# Fritzing sketch termo (saved by Fritzing 0.9.2b)
breadboards: 3

parts:
  Part1 = Arduino Leonardo (Rev3b)
  LED1 = LED - 5mm [color="Yellow (592nm)" package="5 mm [THT]"]
  LED2 = LED - 5mm [color="Yellow (592nm)" package="5 mm [THT]"]
  LED3 = LED - 5mm [color="Yellow (592nm)" package="5 mm [THT]"]
  LED5 = LED - 5mm [color="Yellow (592nm)" package="5 mm [THT]"]
  LED6 = LED - 5mm [color="Yellow (592nm)" package="5 mm [THT]"]
  LED4 = LED - 5mm [color="Yellow (592nm)" package="5 mm [THT]"]
  R2 = Temperature Sensor (Thermistor) [thermistor_type=NTC package=THT]
  R3 = Resistor [tolerance=±5% resistance=2.2k package=THT]
  IC1 = IC, SIP package, 8 pins [chip_label="Resistor net"]

nets:
  N1: Part1.5V, R2.pin_1
  N2: Part1.GND, R3.Pin_1, IC1.pin1
  N3: Part1.A0, R2.pin_0, R3.Pin_0
  N4: Part1.D8/A8, LED6.anode
  N5: Part1.D9_PWM/A9, LED5.anode
  N6: Part1.D10_PWM/A10, LED4.anode
  N7: Part1.D11_PWM, LED3.anode
  N8: Part1.D12/A11, LED2.anode
  N9: Part1.D13_PWM, LED1.anode
  N10: LED1.cathode, IC1.pin3
  N11: LED2.cathode, IC1.pin4
  N12: LED3.cathode, IC1.pin5
  N13: LED5.cathode, IC1.pin7
  N14: LED6.cathode, IC1.pin8
  N15: LED4.cathode, IC1.pin6
